# Fritzing sketch ComfortZoneFan (saved by Fritzing 0.9.3b)

parts:
  BATT1 = 4xAA Switchable Battery Pack w/Bare Wire
  J1 = Power Jack [package=power_jack_slot]
  D1 = Diode [package=diode-1n4001]
  D2 = Diode [package=diode-1n4001]
  M1 = DC Motor
  S1 = SWITCH-SP3T [package=switch-sp3t-smd]

nets:
  N1: BATT1.POS, D1.A
  N2: BATT1.NEG, J1.GNDBREAK, J1.GND, D2.C, S1.1
  N3: J1.PWR, D1.C, M1.pin_1
  N4: D2.A, S1.2
  N5: M1.pin_2, S1.3

notes:
  Fan original wiring

custom parts:
  4xAA Switchable Battery Pack w/Bare Wire: 4xAA Switchable Battery Pack with Bare Wire connection
