# Fritzing sketch ESP8266AlexaComfortZoneUsbFan (saved by Fritzing 0.9.3b)

parts:
  J1 = Power Jack [package=power_jack_slot]
  D1 = Diode [package=diode-1n4001]
  M1 = DC Motor
  WeMos_D1_Mini1 = WeMos D1 Mini
  Q1 = Basic FET N-Channel [package="TO220 [THT]"]
  R2 = Resistor [tolerance=±5% resistance=10k package=THT]
  R1 = Resistor [tolerance=±5% resistance=300 package=THT]

nets:
  N1: J1.GNDBREAK, J1.GND, WeMos_D1_Mini1.G, Q1.source, R2.Pin_1
  N2: J1.PWR, D1.C, M1.pin_1, WeMos_D1_Mini1.5V
  N3: D1.A, M1.pin_2, Q1.drain
  N4: WeMos_D1_Mini1.D2, R2.Pin_0, R1.Pin_1
  N5: Q1.gate, R1.Pin_0

notes:
  Alexa enbled fan
